# Fritzing sketch cEEGOpenBCIConnectorBoard (saved by Fritzing 0.9.4)
circuit board: 1.72cm x 2.62cm
breadboards: 1

parts:
  Pad11 = Pad [width=3 height=1.6 connect=center]
  Pad12 = Pad [width=3 height=1.6 connect=center]
  Pad13 = Pad [width=3 height=1.6 connect=center]
  Pad14 = Pad [width=3 height=1.6 connect=center]
  Pad15 = Pad [width=3 height=1.6 connect=center]
  Pad16 = Pad [width=3 height=1.6 connect=center]
  Pad17 = Pad [width=3 height=1.6 connect=center]
  Pad18 = Pad [width=3 height=1.6 connect=center]
  Pad19 = Pad [width=3 height=1.6 connect=center]
  Pad20 = Pad [width=3 height=1.6 connect=center]
  J5 = double row smd male pin header, 20 pins [form="♂ (male)"]

nets:
  N1: Pad11.pad, J5.pin20
  N2: Pad12.pad, J5.pin19
  N3: Pad13.pad, J5.pin18
  N4: Pad14.pad, J5.pin17
  N5: Pad15.pad, J5.pin16
  N6: Pad16.pad, J5.pin15
  N7: Pad17.pad, J5.pin14
  N8: Pad18.pad, J5.pin13
  N9: Pad19.pad, J5.pin12
  N10: Pad20.pad, J5.pin11
